# Fritzing sketch Mercury2 (saved by Fritzing 0.9.5d)

parts:
  RS485_module1 = RS485 Module (MAX3485)
  WeMos_D1_Mini1 = WeMos D1 Mini
  M1 = RioRand LM2596
  Power_plug1 = Power plug
  J2 = Screw terminal - 2 pins [package=THT]
  M2 = RioRand LM2596

nets:
  N1: RS485_module1.GND, M2.Pin_4
  N2: RS485_module1.A, J2.pin2
  N3: RS485_module1.B, J2.pin1
  N4: RS485_module1.VCC, M2.Pin_3
  N5: RS485_module1.RO, WeMos_D1_Mini1.D1
  N6: RS485_module1.RE, RS485_module1.DE, WeMos_D1_Mini1.D4
  N7: RS485_module1.DI, WeMos_D1_Mini1.D2
  N8: WeMos_D1_Mini1.5V, M1.Pin_3
  N9: WeMos_D1_Mini1.G, M1.Pin_4
  N10: M1.Pin_1, Power_plug1.VCC, M2.Pin_1
  N11: M1.Pin_2, Power_plug1.GND, M2.Pin_2

notes:
  Mercury 206
  A
  B
  +5 VDC
  12 VDC
  3.3 VDC

custom parts:
  RS485 Module (MAX3485): Commercially available RS485 to RS232 TTL Module
