# Fritzing sketch Mercury3 (saved by Fritzing 0.9.5d)

parts:
  RS485_module1 = RS485 Module (MAX3485)
  M1 = RioRand LM2596
  Power_plug1 = Power plug
  J2 = Screw terminal - 2 pins [package=THT]
  M2 = RioRand LM2596
  U1 = ESP8266 ESP-01 Upgraded WiFi Module [part_number=ESP8266]
  R1 = Resistor [tolerance=±5% resistance=220 package="2010 [SMD]"]

nets:
  N1: RS485_module1.GND, M2.Pin_4
  N2: RS485_module1.A, J2.pin2
  N3: RS485_module1.B, J2.pin1
  N4: RS485_module1.VCC, M2.Pin_3
  N5: RS485_module1.RO, U1.RXD
  N6: RS485_module1.RE, RS485_module1.DE, U1.GPIO_0, R1.Pin_0
  N7: RS485_module1.DI, U1.TXD
  N8: M1.Pin_1, Power_plug1.VCC, M2.Pin_1
  N9: M1.Pin_2, Power_plug1.GND, M2.Pin_2
  N10: M1.Pin_3, U1.VCC, R1.Pin_1
  N11: M1.Pin_4, U1.GND

notes:
  Mercury 206
  A
  B
  3.3 VDC
  12 VDC
  10кОм

custom parts:
  RS485 Module (MAX3485): Commercially available RS485 to RS232 TTL Module
  ESP8266 ESP-01 Upgraded WiFi Module: Upgraded Version ESP-01,all Flash are upgraded to 1M byte.Also support Cloud service remote transmission.
