# Fritzing sketch Mercury4 (saved by Fritzing 0.9.5d)

parts:
  M1 = RioRand LM2596
  Power_plug1 = Power plug
  J2 = Screw terminal - 2 pins [package=THT]
  U1 = ESP8266 ESP-01 Upgraded WiFi Module [part_number=ESP8266]
  Component1 = RS485_XY-017 [part_number=XY-017]

nets:
  N1: M1.Pin_1, Power_plug1.VCC
  N2: M1.Pin_2, Power_plug1.GND
  N3: M1.Pin_3, U1.VCC
  GND: M1.Pin_4, U1.GND, Component1.GND
  N4: J2.pin1, Component1.A
  N5: J2.pin2, Component1.B
  N6: U1.RXD, Component1.RXD
  N7: U1.TXD, Component1.TXD

notes:
  Mercury 206
  A
  B
  3.3 VDC
  12 VDC

custom parts:
  ESP8266 ESP-01 Upgraded WiFi Module: Upgraded Version ESP-01,all Flash are upgraded to 1M byte.Also support Cloud service remote transmission.
  RS485_XY-017: Commercially available RS485 to RS232 TTL Module
